# Fritzing sketch Makeev_5SE_fall2017-2 (saved by Fritzing 0.9.4)

parts:
  LCD1 = LCD screen
  A1 = SIM808 module
  S1 = Square Pushbutton
  Part1 = Arduino Uno (Rev3) - ICSP

nets:
  VSS: LCD1.VSS, LCD1.LED+, A1.Pin_3, Part1.5V
  N1: LCD1.V0, Part1.D13/SCK
  N2: LCD1.RS, Part1.ICSP_MISO, Part1.D12/MISO
  N3: LCD1.E, Part1.D9_PWM
  N4: LCD1.DB4, Part1.D4
  N5: LCD1.DB5, Part1.D5_PWM
  N6: LCD1.DB6, Part1.D6_PWM
  N7: LCD1.DB7, Part1.D7
  N8: LCD1.LED-, A1.Pin_4, A1.Pin_13, Part1.GND
  N9: A1.Pin_1, Part1.ICSP_MOSI, Part1.D11_PWM/MOSI
  N10: A1.Pin_2, Part1.D10_PWM/SS
  N11: S1.leg0, Part1.D3_PWM

custom parts:
  SIM808 module: SIM808 Module GSM GPRS GPS Development Board + IPX SMA GSM GPS Antenna Support 2G Network for Arduino Raspberry Pi .
